// Logisim project ex4.circ as structural Verilog: 1 circuit, main circuit Split
module Split (
  input  [7:0] ln1,
  output Out1,
  output [7:0] Out2
);

  not not_1 (Out2[7], ln1[7]);
  and and_1 (Out1, ln1[0], ln1[7]);

  assign Out2[6:0] = ln1[6:0];

  // Notes on the sheet:
  //   PUT CIRCUITRY HERE
endmodule
